// Digital circuit cpu.dig as structural Verilog
module cpu (
  input  Clock
);

  wire instruction_1_p3, instruction_1_p4;
  wire [7:0] pulldown_1_out;
  wire [15:0] instruction_1_p6;

  PullDown #(.Bits(8)) pulldown_1 (.out(pulldown_1_out));
  // instruction instruction_1: pin names not known; wires that end beside it: pulldown_1_out, Clock, instruction_1_p3, instruction_1_p4, pulldown_1_out, instruction_1_p6
  // registers registers_1: pin names not known; wires that end beside it: pulldown_1_out, instruction_1_p3, instruction_1_p4, instruction_1_p6
  PullDown #(.Bits(16)) pulldown_2 (.out(instruction_1_p6));

  // Other names for the same wires on the sheet: CLK = Clock
endmodule
